# Fritzing sketch Montage (saved by Fritzing 0.9.2b)
breadboards: 1

parts:
  U1 = MCP41xxx [package=so08]  # not connected
  Composant1 = Arduino Mega ADK (Rev3)
  J1 = Infrared Proximity Sensor
  Q1 = MOSFET-NCHANNEL [package=to220v]
  VCC1 = Battery  # not connected

nets:
  N1: Composant1.A9, J1.Vout
  GND: Composant1.GND, J1.GND, Q1.S
  5V: Composant1.5V, J1.Vcc
